# Fritzing sketch GameCube_Pendant_JOG_Adapter (saved by Fritzing 0.9.3b)

parts:
  Part2 = Logic Level Converter
  C2 = Electrolytic Capacitor [capacitance=33µF package="100 mil [THT, electrolytic]"]
  R2 = Resistor [tolerance=±5% resistance=1k package=THT]
  CNCUSB_MK1_Jog_header = shrouded pin header, 26 pins [form="♂ (shrouded male)"]
  R1 = Resistor [tolerance=±5% resistance=1k package=THT]
  Part3 = Arduino Nano (Rev3.0)
  Gamecube_Controller = longpad pin header, 5 pins [form="long pad"]

nets:
  N1: Part2.TX2_LV, R2.Pin_1, Gamecube_Controller.pin4
  GND: Part2.GND, C2.-, CNCUSB_MK1_Jog_header.pin6, Part3.GND, Gamecube_Controller.pin1
  N2: Part2.LV, R2.Pin_0, Part3.3V3, Gamecube_Controller.pin5
  N3: Part2.HV, Part3.5V
  N4: Part2.TX2_HV, Part3.D13/SCK
  N5: C2.+, CNCUSB_MK1_Jog_header.pin22, R1.Pin_0
  N6: CNCUSB_MK1_Jog_header.pin7, Part3.D2
  N7: CNCUSB_MK1_Jog_header.pin8, Part3.D4
  N8: CNCUSB_MK1_Jog_header.pin9, Part3.D6
  N9: CNCUSB_MK1_Jog_header.pin10, Part3.D8
  N10: CNCUSB_MK1_Jog_header.pin17, Part3.D9
  N11: CNCUSB_MK1_Jog_header.pin18, Part3.D7
  N12: CNCUSB_MK1_Jog_header.pin19, Part3.D5
  N13: CNCUSB_MK1_Jog_header.pin20, Part3.D3
  N14: CNCUSB_MK1_Jog_header.pin21, Part3.VIN
  N15: R1.Pin_1, Part3.D10

notes:
  GND | motor(GND | 5V) |  DATA | 3.3v
  Can use 5V from Jog controller to power the arduino
